# Fritzing sketch SpectrumSeteliteToArduinoTest (saved by Fritzing 0.4.3b)
breadboards: 1

parts:
  U1 = atmega168 [package="DIP28 [THT]"]
  Arduino1 = Arduino
  J1 = female pin header, 14 pins [form="♀ (female)"]
  J1_2 = female pin header, 14 pins [form="♀ (female)"]  # not connected
  R1 = Resistor [resistance=10k package=THT]
  J2 = female pin header, 3 pins [form="♀ (female)"]

nets:
  N1: U1.Pin_1, Arduino1.RST, R1.Pin_0
  N2: U1.Pin_2, J2.pin3
  N3: U1.Pin_3, Arduino1.D1TX
  N4: U1.Pin_7, U1.Pin_20, Arduino1.+5V, R1.Pin_1
  N5: U1.Pin_8, U1.Pin_22, Arduino1.GND, J2.pin2
  N6: U1.Pin_9, J1.pin6
  N7: U1.Pin_10, J1.pin5
  N8: Arduino1.3V3, J2.pin1

notes:
  Reciver
